# Fritzing sketch Schematics (saved by Fritzing 0.9.3b)
breadboards: 1

parts:
  R2 = Resistor [tolerance=±5% resistance=2.7k package=THT]
  R1 = Resistor [tolerance=±5% resistance=2.7k package=THT]
  R4 = Resistor [tolerance=±5% resistance=2.7k package=THT]
  R5 = Resistor [tolerance=±5% resistance=2.7k package=THT]
  R6 = Resistor [tolerance=±5% resistance=2.7k package=THT]
  R7 = Resistor [tolerance=±5% resistance=2.7k package=THT]
  R40 = Resistor [tolerance=±5% resistance=2.7k package=THT]
  R14 = Resistor [tolerance=±5% resistance=2.7k package=THT]
  R9 = Resistor [tolerance=±5% resistance=2.7k package=THT]
  R15 = Resistor [tolerance=±5% resistance=2.7k package=THT]
  R13 = Resistor [tolerance=±5% resistance=2.7k package=THT]
  R10 = Resistor [tolerance=±5% resistance=2.7k package=THT]
  R16 = Resistor [tolerance=±5% resistance=2.7k package=THT]
  R12 = Resistor [tolerance=±5% resistance=2.7k package=THT]
  R17 = Resistor [tolerance=±5% resistance=56k package=THT]
  R18 = Resistor [tolerance=±5% resistance=56k package=THT]
  R19 = Resistor [tolerance=±5% resistance=56k package=THT]
  R20 = Resistor [tolerance=±5% resistance=56k package=THT]
  R21 = Resistor [tolerance=±5% resistance=56k package=THT]
  R22 = Resistor [tolerance=±5% resistance=56k package=THT]
  R23 = Resistor [tolerance=±5% resistance=56k package=THT]
  R24 = Resistor [tolerance=±5% resistance=56k package=THT]
  R25 = Resistor [tolerance=±5% resistance=56k package=THT]
  R26 = Resistor [tolerance=±5% resistance=56k package=THT]
  R27 = Resistor [tolerance=±5% resistance=56k package=THT]
  R28 = Resistor [tolerance=±5% resistance=56k package=THT]
  R29 = Resistor [tolerance=±5% resistance=56k package=THT]
  R30 = Resistor [tolerance=±5% resistance=56k package=THT]
  R31 = Resistor [tolerance=±5% resistance=56k package=THT]
  R32 = Resistor [tolerance=±5% resistance=56k package=THT]
  R3 = Resistor [tolerance=±5% resistance=2.7k package=THT]
  R33 = Resistor [tolerance=±5% resistance=2.7k package=THT]
  R34 = Resistor [tolerance=±5% resistance=150 package=THT]
  R35 = Resistor [tolerance=±5% resistance=150 package=THT]
  R36 = Resistor [tolerance=±5% resistance=150 package=THT]
  R37 = Resistor [tolerance=±5% resistance=150 package=THT]
  R38 = Resistor [tolerance=±5% resistance=150 package=THT]
  R39 = Resistor [tolerance=±5% resistance=150 package=THT]
  8×IR_LED = LTE-302 [package=lte-302]
  D40 = LTE-302 [package=lte-302]
  D41 = LTE-302 [package=lte-302]
  D42 = LTE-302 [package=lte-302]
  D43 = LTE-302 [package=lte-302]
  D44 = LTE-302 [package=lte-302]
  D45 = LTE-302 [package=lte-302]
  D46 = LTE-302 [package=lte-302]
  D47 = LTE-302 [package=lte-302]
  D48 = LTE-302 [package=lte-302]
  D49 = LTE-302 [package=lte-302]
  D50 = LTE-302 [package=lte-302]
  D51 = LTE-302 [package=lte-302]
  D52 = LTE-302 [package=lte-302]
  D54 = LTE-302 [package=lte-302]
  8×IR_LED_2 = LTE-302 [package=lte-302]
  Arduino_Mega_Board = Arduino Mega 2560 (Rev3)
  16×2_LCD_with_i2c_backpack = LCD1602-I2C
  Wire_to_Board_Terminal = Camdenboss CTB0158-8 [part_number=CTB0158-8 package=THT]
  Wire_to_Board_Terminal_2 = Camdenboss CTB0158-8 [part_number=CTB0158-8 package=THT]
  Wire_to_Board_Terminal_3 = Camdenboss CTB0158-8 [part_number=CTB0158-8 package=THT]
  Wire_to_Board_Terminal_4 = Camdenboss CTB0158-8 [part_number=CTB0158-8 package=THT]
  Q12 = LTR-301 [package=ltr-301]
  Q28 = LTR-301 [package=ltr-301]
  8×IR_Phototransistor = LTR-301 [package=ltr-301]
  Q30 = LTR-301 [package=ltr-301]
  Q31 = LTR-301 [package=ltr-301]
  Q32 = LTR-301 [package=ltr-301]
  Q43 = LTR-301 [package=ltr-301]
  Q34 = LTR-301 [package=ltr-301]
  8×IR_Phototransistor_2 = LTR-301 [package=ltr-301]
  Q36 = LTR-301 [package=ltr-301]
  Q37 = LTR-301 [package=ltr-301]
  Q38 = LTR-301 [package=ltr-301]
  Q39 = LTR-301 [package=ltr-301]
  Q40 = LTR-301 [package=ltr-301]
  Q41 = LTR-301 [package=ltr-301]
  Q42 = LTR-301 [package=ltr-301]
  5V = 4 x AAA Battery Mount

nets:
  N1: R2.Pin_0, Wire_to_Board_Terminal_2.pin8
  N2: R2.Pin_1, R1.Pin_1, R4.Pin_1, R5.Pin_1, R6.Pin_1, R7.Pin_1, R40.Pin_1, R14.Pin_1, R9.Pin_1, R15.Pin_1, R13.Pin_1, R10.Pin_1, R16.Pin_1, R12.Pin_1, R3.Pin_1, R33.Pin_1, R34.Pin_0, R35.Pin_1, R36.Pin_0, R37.Pin_1, R38.Pin_0, R39.Pin_0, 5V.+
  N3: R1.Pin_0, Wire_to_Board_Terminal_2.pin7
  N4: R4.Pin_0, Wire_to_Board_Terminal_2.pin6
  N5: R5.Pin_0, Wire_to_Board_Terminal_2.pin5
  N6: R6.Pin_0, Wire_to_Board_Terminal.pin7
  N7: R7.Pin_0, Wire_to_Board_Terminal.pin8
  N8: R40.Pin_0, Wire_to_Board_Terminal_2.pin1
  N9: R14.Pin_0, Wire_to_Board_Terminal_2.pin2
  N10: R9.Pin_0, Wire_to_Board_Terminal.pin4
  N11: R15.Pin_0, Wire_to_Board_Terminal_2.pin3
  N12: R13.Pin_0, Wire_to_Board_Terminal.pin6
  N13: R10.Pin_0, Wire_to_Board_Terminal.pin3
  N14: R16.Pin_0, Wire_to_Board_Terminal_2.pin4
  N15: R12.Pin_0, Wire_to_Board_Terminal.pin5
  N16: R17.Pin_0, Arduino_Mega_Board.A15, Wire_to_Board_Terminal_4.pin8
  GND: R17.Pin_1, R18.Pin_1, R19.Pin_1, R20.Pin_1, R21.Pin_1, R22.Pin_1, R23.Pin_1, R24.Pin_1, R25.Pin_1, R26.Pin_1, R27.Pin_1, R28.Pin_1, R29.Pin_1, R30.Pin_1, R31.Pin_1, R32.Pin_1, D42.C, D49.C, Arduino_Mega_Board.GND, 16×2_LCD_with_i2c_backpack.GND, 5V.-
  N17: R18.Pin_0, Arduino_Mega_Board.A14, Wire_to_Board_Terminal_4.pin7
  N18: R19.Pin_0, Arduino_Mega_Board.A12, Wire_to_Board_Terminal_4.pin5
  N19: R20.Pin_0, Arduino_Mega_Board.A13, Wire_to_Board_Terminal_4.pin6
  N20: R21.Pin_0, Arduino_Mega_Board.A9, Wire_to_Board_Terminal_4.pin2
  N21: R22.Pin_0, Arduino_Mega_Board.A8, Wire_to_Board_Terminal_4.pin1
  N22: R23.Pin_0, Arduino_Mega_Board.A10, Wire_to_Board_Terminal_4.pin3
  N23: R24.Pin_0, Arduino_Mega_Board.A11, Wire_to_Board_Terminal_4.pin4
  N24: R25.Pin_0, Arduino_Mega_Board.A2, Wire_to_Board_Terminal_3.pin3
  N25: R26.Pin_0, Arduino_Mega_Board.A1, Wire_to_Board_Terminal_3.pin2
  N26: R27.Pin_0, Arduino_Mega_Board.A5, Wire_to_Board_Terminal_3.pin6
  N27: R28.Pin_0, Arduino_Mega_Board.A0, Wire_to_Board_Terminal_3.pin1
  N28: R29.Pin_0, Arduino_Mega_Board.A4, Wire_to_Board_Terminal_3.pin5
  N29: R30.Pin_0, Arduino_Mega_Board.A6, Wire_to_Board_Terminal_3.pin7
  N30: R31.Pin_0, Arduino_Mega_Board.A7, Wire_to_Board_Terminal_3.pin8
  N31: R32.Pin_0, Arduino_Mega_Board.A3, Wire_to_Board_Terminal_3.pin4
  N32: R3.Pin_0, Wire_to_Board_Terminal.pin2
  N33: R33.Pin_0, Wire_to_Board_Terminal.pin1
  N34: R34.Pin_1, R35.Pin_0, R36.Pin_1, D52.A
  N35: R37.Pin_0, R38.Pin_1, R39.Pin_1, D41.A
  N36: 8×IR_LED.A, D40.C
  N37: 8×IR_LED.C, D45.A
  N38: D40.A, D46.C
  N39: D41.C, D46.A
  N40: D42.A, D44.C
  N41: D43.A, D45.C
  N42: D43.C, D44.A
  N43: D47.A, D50.C
  N44: D47.C, D54.A
  N45: D48.A, D51.C
  N46: D48.C, 8×IR_LED_2.A
  N47: D49.A, D54.C
  N48: D50.A, 8×IR_LED_2.C
  N49: D51.A, D52.C
  N50: Arduino_Mega_Board.D21/SCL, Arduino_Mega_Board.SCL, 16×2_LCD_with_i2c_backpack.SCL
  N51: Arduino_Mega_Board.D20/SDA, Arduino_Mega_Board.SDA, 16×2_LCD_with_i2c_backpack.SDA
  VIN: Arduino_Mega_Board.VIN, 16×2_LCD_with_i2c_backpack.VCC
  N52: Wire_to_Board_Terminal.terminal_1, Q39.E
  N53: Wire_to_Board_Terminal.terminal_2, Q36.E
  N54: Wire_to_Board_Terminal.terminal_3, Q38.E
  N55: Wire_to_Board_Terminal.terminal_4, 8×IR_Phototransistor_2.E
  N56: Wire_to_Board_Terminal.terminal_5, Q40.E
  N57: Wire_to_Board_Terminal.terminal_6, Q42.E
  N58: Wire_to_Board_Terminal.terminal_7, Q41.E
  N59: Wire_to_Board_Terminal.terminal_8, Q37.E
  N60: Wire_to_Board_Terminal_2.terminal_1, Q43.E
  N61: Wire_to_Board_Terminal_2.terminal_2, Q34.E
  N62: Wire_to_Board_Terminal_2.terminal_3, Q32.E
  N63: Wire_to_Board_Terminal_2.terminal_4, Q31.E
  N64: Wire_to_Board_Terminal_2.terminal_5, 8×IR_Phototransistor.E
  N65: Wire_to_Board_Terminal_2.terminal_6, Q30.E
  N66: Wire_to_Board_Terminal_2.terminal_7, Q28.E
  N67: Wire_to_Board_Terminal_2.terminal_8, Q12.E
  N68: Wire_to_Board_Terminal_3.terminal_1, Q39.C
  N69: Wire_to_Board_Terminal_3.terminal_2, Q36.C
  N70: Wire_to_Board_Terminal_3.terminal_3, Q38.C
  N71: Wire_to_Board_Terminal_3.terminal_4, 8×IR_Phototransistor_2.C
  N72: Wire_to_Board_Terminal_3.terminal_5, Q40.C
  N73: Wire_to_Board_Terminal_3.terminal_6, Q42.C
  N74: Wire_to_Board_Terminal_3.terminal_7, Q41.C
  N75: Wire_to_Board_Terminal_3.terminal_8, Q37.C
  N76: Wire_to_Board_Terminal_4.terminal_1, Q43.C
  N77: Wire_to_Board_Terminal_4.terminal_2, Q34.C
  N78: Wire_to_Board_Terminal_4.terminal_3, Q32.C
  N79: Wire_to_Board_Terminal_4.terminal_4, Q31.C
  N80: Wire_to_Board_Terminal_4.terminal_5, 8×IR_Phototransistor.C
  N81: Wire_to_Board_Terminal_4.terminal_6, Q30.C
  N82: Wire_to_Board_Terminal_4.terminal_7, Q28.C
  N83: Wire_to_Board_Terminal_4.terminal_8, Q12.C

custom parts:
  LCD1602-I2C: A standard character display, usually with 2x16 characters. Comes in many colors with LCM1602 IIC attached.
